# Fritzing sketch Pepshow (saved by Fritzing 0.9.3b)
breadboards: 1

parts:
  Part1 = Coin Acceptor - 6-Coin version
  tft1 = 3.2in tft touch screen
  Raspberry_Pi_1 = Raspberry Pi 3 [part_number=RPI-3-V1.2]
  JACK1 = 2.1mm Barrel Jack with Terminal Block
  J1 = SO08-EIAJ [package=SO]
  BUTTON1 = Arcade Button (white)
  R1 = Resistor [tolerance=±5% resistance=220 package=THT]

nets:
  N1: Part1.GND, JACK1.NEG
  N2: Part1.SIG, R1.Pin_1
  N3: Part1.12V, JACK1.POS
  N4: tft1.GND, J1.4
  N5: tft1.VCC, J1.1
  N6: tft1.LCD_DB0, J1.3
  N7: tft1.LCD_DB1, J1.2
  N8: Raspberry_Pi_1.GPIO12, R1.Pin_0
  N9: Raspberry_Pi_1.GND, BUTTON1.no_name_yet#2
  N10: Raspberry_Pi_1.ID_SC, BUTTON1.no_name_yet#1

notes:
  Coin Acceptor, 12v in
  Start
  Disply Wiring

custom parts:
  Coin Acceptor - 6-Coin version: 12V coin acceptor that can handle up to 6 different denominations. Output is either pulse width, serial, or single pin per coin value.
  3.2in tft touch screen: 3.2" tft touch screen lcd display
  Arcade Button (white): Adafruit Arcade Button (white)
